# Fritzing sketch rp2040_schematic (saved by Fritzing 0.9.3b)

parts:
  Mod1 = Raspberry Pi Pico
  RE1 = Rotary Encoder [package=THT]
  S1 = Pushbutton [package="[THT]"]
  S2 = Pushbutton [package="[THT]"]
  Bauteil1 = OLED Monochrome 128x64 1.3 inch [part_number=938]
  R1 = Rotary Potentiometer (Small) [maximum_resistance=100kΩ package=THT]
  R2 = Rotary Potentiometer (Small) [maximum_resistance=100kΩ package=THT]
  R3 = Rotary Potentiometer (Small) [maximum_resistance=100kΩ package=THT]
  I2S_Interface = female pin header, 5 pins [form="♀ (female)"]
  U1 = Voltage Regulator - 5V [package="TO220 [THT]"]
  9V_Power_Supply = Power Jack [package=power_jack_combo]
  C1 = Ceramic Capacitor [capacitance=100nF package="100 mil [THT, multilayer]"]
  C2 = Ceramic Capacitor [capacitance=100nF package="100 mil [THT, multilayer]"]
  Q1 = NPN-Transistor [part_number=2N3904 package="TO92 [THT]"]
  LED1 = LED - 5mm [color="Green (565nm)" package="5 mm [THT]"]
  LED2 = LED - 5mm [color="White (6500K)" package="5 mm [THT]"]
  R4 = Trimmer Potentiometer [maximum_resistance=10kΩ package=THT]
  R5 = Resistor [tolerance=±5% resistance=120 package=THT]
  R6 = Resistor [tolerance=±5% resistance=39k package=THT]
  IC1 = Dual Op-Amp [package=dip08]
  R7 = Resistor [tolerance=±1% resistance=1M package="2010 [SMD]"]
  R8 = Resistor [tolerance=±1% resistance=4.7k package="2010 [SMD]"]
  R9 = Resistor [tolerance=±1% resistance=2.2k package="2010 [SMD]"]
  C3 = Electrolytic Capacitor [capacitance=1µF package="100 mil [THT, electrolytic]"]
  C4 = Electrolytic Capacitor [capacitance=1µF package="100 mil [THT, electrolytic]"]
  Guitar_Input = AUDIO-JACK2 [package=audio-jack]
  C5 = Electrolytic Capacitor [capacitance=1µF package="100 mil [THT, electrolytic]"]
  R10 = Rotary Potentiometer (Small) [maximum_resistance=10kΩ package=THT]

nets:
  GND: Mod1.pin_3, Mod1.pin_18, Mod1.pin_23, Mod1.pin_33, Mod1.pin_38, Mod1.pin_42, RE1.EncoderPinC, S1.Pin_2, S2.Pin_1, S2.Pin_2, Bauteil1.GND, R1.leg1, R2.leg1, R3.leg1, U1.GND, 9V_Power_Supply.GND, C1.0, C2.0, LED2.cathode, IC1.A_V-, C3.-, Guitar_Input.SLEEVE, R10.leg1
  N1: Mod1.pin_9, RE1.EncoderPinA
  N2: Mod1.pin_10, RE1.EncoderPinB
  N3: Mod1.pin_11, I2S_Interface.pin5
  N4: Mod1.pin_12, I2S_Interface.pin3
  N5: Mod1.pin_14, I2S_Interface.pin4
  N6: Mod1.pin_15, I2S_Interface.pin1
  N7: Mod1.pin_16, I2S_Interface.pin2
  N8: Mod1.pin_19, Bauteil1.DC_SA0
  N9: Mod1.pin_20, Bauteil1.RESET
  N10: Mod1.pin_24, Bauteil1.SCLK_SCK
  N11: Mod1.pin_25, Bauteil1.MOSI_SDA
  N12: Mod1.pin_26, S2.Pin_3, S2.Pin_4
  N13: Mod1.pin_27, Bauteil1.CS
  N14: Mod1.pin_29, S1.Pin_3
  N15: Mod1.pin_31, R1.wiper
  N16: Mod1.pin_32, R2.wiper
  N17: Mod1.pin_34, R3.wiper
  3.3V: Mod1.pin_36, Bauteil1.3.3V, R1.leg2, R2.leg2, R3.leg2
  5V: Mod1.pin_39, U1.output_voltage, C2.1
  N18: U1.input_voltage, 9V_Power_Supply.PWR, C1.1, R4.leg2, R5.Pin_0, IC1.A_V+
  N19: Q1.E, LED1.anode, IC1.A_+IN
  N20: Q1.B, R6.Pin_1
  N21: Q1.C, R5.Pin_1
  N22: LED1.cathode, LED2.anode
  N23: R4.leg1, R4.wiper, R6.Pin_0
  N24: IC1.A_OUT, IC1.A_-IN, R7.Pin_0
  N25: IC1.B_+IN, R7.Pin_1, C4.+
  N26: IC1.B_-IN, R8.Pin_1, R9.Pin_0
  N27: IC1.B_OUT, R8.Pin_0, C5.+
  N28: R9.Pin_1, C3.+
  N29: C4.-, Guitar_Input.TIP
  N30: C5.-, R10.leg2
  ADC Input: R10.wiper

notes:
  BCLK
  LRCLK
  Data in
  Data out
  MCLK
  roughly 4.5v reference

custom parts:
  Raspberry Pi Pico: Raspberry Pi Pico. Based around the RP2040 microcontroller the Pico is a low cost microcontroller device bringing Raspberry Pi quality, cost, and easy of use to the microcontroller space. Jan 2021, Split part in to two versions: tht (this one) and SMD. This one will drill holes for a .1 in header in pcb to allow plugging in the module as well as providing pads to solder the module to the top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
  OLED Monochrome 128x64 1.3 inch: These displays are small, only about 1.3" diagonal, but very readable due to the high contrast of an OLED display. This display is made of 128x64 individual white OLED pixels, each one is turned on or off by the controller chip. Because the display makes its own light, no backlight is required. This reduces the power required to run the OLED and is why the display has such high contrast; we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
