# Fritzing sketch rp2040_schematic (saved by Fritzing 0.9.6b)

parts:
  Mod1 = Raspberry Pi Pico
  RE1 = Rotary Encoder [package=THT]
  S1 = Pushbutton [package="[THT]"]
  S2 = Pushbutton [package="[THT]"]
  Bauteil1 = OLED Monochrome 128x64 1.3 inch [part_number=938]
  R1 = Rotary Potentiometer (Small) [maximum_resistance=100kΩ package=THT]
  R2 = Rotary Potentiometer (Small) [maximum_resistance=100kΩ package=THT]
  R3 = Rotary Potentiometer (Small) [maximum_resistance=100kΩ package=THT]
  I2S_Interface = female pin header, 5 pins [form="♀ (female)"]
  12V_Power_Supply = Power Jack [package=power_jack_combo]
  C1 = Ceramic Capacitor [capacitance=100nF package="100 mil [THT, multilayer]"]
  C2 = Ceramic Capacitor [capacitance=100nF package="100 mil [THT, multilayer]"]
  IC1 = Dual Op-Amp [package=dip08]
  R7 = Resistor [tolerance=±1% resistance=1M package="2010 [SMD]"]
  R8 = Resistor [tolerance=±1% resistance=4.7k package="2010 [SMD]"]
  R9 = Resistor [tolerance=±1% resistance=2.2k package="2010 [SMD]"]
  C3 = Electrolytic Capacitor [capacitance=1µF package="100 mil [THT, electrolytic]"]
  C4 = Electrolytic Capacitor [capacitance=1µF package="100 mil [THT, electrolytic]"]
  Guitar_Input = AUDIO-JACK2 [package=audio-jack]
  C5 = Electrolytic Capacitor [capacitance=1µF package="100 mil [THT, electrolytic]"]
  R10 = Rotary Potentiometer (Small) [maximum_resistance=10kΩ package=THT]
  U1 = Voltage Regulator - Variable [package="TO220 [THT]"]
  IC2 = Voltage Regulator [package=to-92]
  IC3 = Voltage Regulator [package=to-92]
  C6 = Ceramic Capacitor [capacitance=100nF voltage=35V package="100 mil [THT, multilayer]"]
  C7 = Ceramic Capacitor [capacitance=100nF voltage=35V package="100 mil [THT, multilayer]"]
  Input_Clipping = smd LED [color="Red (633nm)" package="0805 [SMD]"]
  R11 = Resistor [tolerance=±5% power=0.25 resistance=180 package=THT]
  Output_Clipping = smd LED [color="Red (633nm)" package="0805 [SMD]"]
  R12 = Resistor [tolerance=±5% power=0.25 resistance=180 package=THT]

nets:
  GND: Mod1.pin_3, Mod1.pin_8, Mod1.pin_13, Mod1.pin_18, Mod1.pin_23, Mod1.pin_33, Mod1.pin_38, Mod1.pin_42, RE1.EncoderPinC, S1.Pin_1, S1.Pin_2, S2.Pin_1, S2.Pin_2, Bauteil1.GND, R1.leg1, R2.leg1, R3.leg1, 12V_Power_Supply.GND, C1.0, C2.0, IC1.A_V-, C3.-, Guitar_Input.SLEEVE, R10.leg1, IC2.GND, IC3.GND, C6.0, C7.0, Input_Clipping.cathode, Output_Clipping.cathode
  N1: Mod1.pin_9, RE1.EncoderPinA
  N2: Mod1.pin_10, RE1.EncoderPinB
  N3: Mod1.pin_11, I2S_Interface.pin5
  N4: Mod1.pin_12, I2S_Interface.pin3
  N5: Mod1.pin_14, I2S_Interface.pin4
  N6: Mod1.pin_15, I2S_Interface.pin1
  N7: Mod1.pin_16, I2S_Interface.pin2
  N8: Mod1.pin_19, Bauteil1.DC_SA0
  N9: Mod1.pin_20, Bauteil1.RESET
  N10: Mod1.pin_21, R11.Pin_0
  N11: Mod1.pin_22, R12.Pin_0
  N12: Mod1.pin_24, Bauteil1.SCLK_SCK
  N13: Mod1.pin_25, Bauteil1.MOSI_SDA
  N14: Mod1.pin_26, S2.Pin_3, S2.Pin_4
  N15: Mod1.pin_27, Bauteil1.CS
  N16: Mod1.pin_29, S1.Pin_3
  N17: Mod1.pin_31, R1.wiper
  N18: Mod1.pin_32, R2.wiper
  N19: Mod1.pin_34, R3.wiper
  3.3V: Mod1.pin_36, Bauteil1.3.3V, R1.leg2, R2.leg2, R3.leg2
  Vsys: Mod1.pin_39, IC2.OUT, C7.1
  N20: 12V_Power_Supply.PWR, C1.1, U1.IN
  N21: IC1.A_OUT, IC1.A_-IN, R7.Pin_0
  N22: IC1.A_+IN, IC3.OUT
  N23: IC1.B_+IN, R7.Pin_1, C4.+
  N24: IC1.B_-IN, R8.Pin_1, R9.Pin_0
  N25: IC1.B_OUT, R8.Pin_0, C5.+
  N26: R9.Pin_1, C3.+
  N27: C4.-, Guitar_Input.TIP
  N28: C5.-, R10.leg2
  ADC Input (L): R10.wiper
  N29: U1.OUT, IC2.IN, IC3.IN, C6.1
  N30: Input_Clipping.anode, R11.Pin_1
  N31: Output_Clipping.anode, R12.Pin_1

notes:
  BCLK
  Data out
  Data in
  LRCLK
  MCLK

custom parts:
  Raspberry Pi Pico: Raspberry Pi Pico. Based around the RP2040 microcontroller the Pico is a low cost microcontroller device bringing Raspberry Pi quality, cost, and easy of use to the microcontroller space. Jan 2021, Split part in to two versions: tht (this one) and SMD. This one will drill holes for a .1 in header in pcb to allow plugging in the module as well as providing pads to solder the module to the top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
  OLED Monochrome 128x64 1.3 inch: These displays are small, only about 1.3" diagonal, but very readable due to the high contrast of an OLED display. This display is made of 128x64 individual white OLED pixels, each one is turned on or off by the controller chip. Because the display makes its own light, no backlight is required. This reduces the power required to run the OLED and is why the display has such high contrast; we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
